# Fritzing sketch ControlPanel (saved by Fritzing 0.9.0b)
circuit board: 8.46667cm x 5.64444cm
breadboards: 1

parts:
  U1 = MAX7219 [package=dil24]  # not connected
  U2 = MAX7219 [package=dil24]  # not connected
  U3 = MAX7219 [package=dil24]  # not connected
  Raspberry_Pi_3 = Raspberry Pi 3
  S1 = Toggle Switch [package=THT]
  S2 = Toggle Switch [package=THT]
  S3 = Toggle Switch [package=THT]
  R1 = Resistor [tolerance=±5% resistance=220 package=THT]
  R2 = Resistor [tolerance=±5% resistance=220 package=THT]
  R3 = Resistor [tolerance=±5% resistance=220 package=THT]

nets:
  3V3: Raspberry_Pi_3.3v3, Raspberry_Pi_3.3V3, S1.COM, S2.COM, S3.COM
  N1: Raspberry_Pi_3.GIPO25, R1.Pin_0
  N2: Raspberry_Pi_3.GIPO24, R2.Pin_0
  N3: Raspberry_Pi_3.GIPO23, R3.Pin_0
  N4: S1.L2, R1.Pin_1
  N5: S2.L2, R2.Pin_1
  N6: S3.L2, R3.Pin_1
